# Fritzing sketch dht11_7seg (saved by Fritzing 0.9.3b)
breadboards: 1

parts:
  Mod1 = Raspberry Pi Pico
  7_Segment_4_Digit_Display2 = 7-SEGMENT-4DIGIT common cathode [part_number=HS420561K-32 package=7-segment-4digit-cathode]
  DHT1 = DHT11 Humitidy and Temperature Sensor (3 pins)
  R1 = Resistor [tolerance=±5% resistance=10 package="0603 [SMD]"]
  R2 = Resistor [tolerance=±5% resistance=10 package="0603 [SMD]"]
  R3 = Resistor [tolerance=±5% resistance=10 package="0603 [SMD]"]
  R4 = Resistor [tolerance=±5% resistance=10 package="0603 [SMD]"]
  R5 = Resistor [tolerance=±5% resistance=10 package="0603 [SMD]"]
  R6 = Resistor [tolerance=±5% resistance=5.6k package="0603 [SMD]"]

nets:
  N1: Mod1.pin_3, Mod1.pin_8, Mod1.pin_13, Mod1.pin_18, Mod1.pin_23, Mod1.pin_28, Mod1.pin_33, Mod1.pin_38, DHT1.GND
  N2: Mod1.pin_7, R1.Pin_0
  N3: Mod1.pin_14, 7_Segment_4_Digit_Display2.pin_7
  N4: Mod1.pin_15, 7_Segment_4_Digit_Display2.pin_8
  N5: Mod1.pin_16, 7_Segment_4_Digit_Display2.pin_9
  N6: Mod1.pin_17, 7_Segment_4_Digit_Display2.pin_10
  N7: Mod1.pin_19, 7_Segment_4_Digit_Display2.pin_11
  N8: Mod1.pin_20, 7_Segment_4_Digit_Display2.pin_12
  N9: Mod1.pin_21, 7_Segment_4_Digit_Display2.pin_1
  N10: Mod1.pin_22, 7_Segment_4_Digit_Display2.pin_2
  N11: Mod1.pin_24, 7_Segment_4_Digit_Display2.pin_4
  N12: Mod1.pin_25, 7_Segment_4_Digit_Display2.pin_5
  N13: Mod1.pin_26, 7_Segment_4_Digit_Display2.pin_6
  N14: Mod1.pin_27, 7_Segment_4_Digit_Display2.pin_3
  N15: Mod1.pin_36, DHT1.DATA, R6.Pin_1
  N16: R1.Pin_1, R2.Pin_0
  N17: R2.Pin_1, R3.Pin_0
  N18: R3.Pin_1, R4.Pin_0
  N19: R4.Pin_1, R5.Pin_0
  N20: R5.Pin_1, R6.Pin_0

custom parts:
  Raspberry Pi Pico: Raspberry Pi Pico. Based around the RP2040 microcontroller the Pico is a low cost microcontroller device bringing Raspberry Pi quality, cost, and easy of use to the microcontroller space. Jan 2021, Split part in to two versions: tht (this one) and SMD. This one will drill holes for a .1 in header in pcb to allow plugging in the module as well as providing pads to solder the module to the top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
  7-SEGMENT-4DIGIT common cathode: A 7 Segment 4 Digit common cathode display, with decimal points
  DHT11 Humitidy and Temperature Sensor (3 pins): DHT11 Humidity and Temperature Sensor (3 pins) from the design created by John De Cristofaro for Adafruit Industries.
